// Logisim project A'+BC_KK.circ as structural Verilog: 1 circuit, main circuit main
module main (
  input  A,
  input  B,
  input  C,
  output A_prime___BC
);

  wire BC_out, not_1_out;

  not not_1 (not_1_out, A);
  and BC (BC_out, B, C);
  or or_1 (A_prime___BC, not_1_out, BC_out);

  // Notes on the sheet:
  //   A'
  //   Kara Kohutek
  //   Lab 2 - Introduction to Boolean Equations and Ciruits
  //   Task 2 circuit diagram
  //   Result
endmodule
