// Logisim project Assigment5.circ as structural Verilog: 3 circuits, main circuit main
module main (
  input  in_1,
  input  in_2,
  input  in_3,
  input  in_4
);

  wire decoder_1_out0, decoder_1_out1, decoder_1_out2, decoder_1_out3, decoder_1_out4, decoder_1_out5,
       decoder_1_out6, decoder_1_out7, decoder_1_out8, decoder_1_out9;

  Decoder #(.select(4)) decoder_1 (
    .out0(decoder_1_out0), .out1(decoder_1_out1), .out2(decoder_1_out2), .out3(decoder_1_out3),
    .out4(decoder_1_out4), .out5(decoder_1_out5), .out6(decoder_1_out6), .out7(decoder_1_out7),
    .out8(decoder_1_out8), .out9(decoder_1_out9), .en(in_1));  // open: out10, out11, out12, out13, out14, out15, sel

  assign in_2 = in_1;
  assign in_3 = in_1;
  assign in_4 = in_1;
endmodule

module Assigment5 (
  input  A,
  input  B,
  input  C,
  input  D,
  output W,
  output X,
  output Y,
  output Z
);

  wire and_1_out, and_2_out, and_3_out, and_4_out, and_5_out, and_6_out, and_7_out, and_8_out, and_9_out,
       and_10_out, not_1_out, not_2_out, not_3_out, not_4_out, not_5_out, not_6_out, not_7_out, not_8_out,
       not_9_out, not_10_out;

  not not_1 (not_1_out, A);
  and and_1 (and_1_out, not_1_out, D);
  and and_2 (and_2_out, A, not_2_out);
  not not_2 (not_2_out, D);
  not not_3 (not_3_out, A);
  not not_4 (not_4_out, C);
  and and_3 (and_3_out, not_3_out, not_4_out, not_5_out);
  not not_5 (not_5_out, D);
  and and_4 (and_4_out, C, D);
  and and_5 (and_5_out, B, not_6_out);
  not not_6 (not_6_out, D);
  and and_6 (and_6_out, A, D);
  not not_7 (not_7_out, C);
  and and_7 (and_7_out, not_7_out, not_8_out);
  not not_8 (not_8_out, D);
  and and_8 (and_8_out, B, D);
  not not_9 (not_9_out, B);
  and and_9 (and_9_out, not_9_out, not_10_out);
  not not_10 (not_10_out, D);
  and and_10 (and_10_out, B, C);
  or or_1 (W, and_1_out, C, B, and_2_out);
  or or_2 (X, and_3_out, and_4_out, and_5_out, and_6_out);
  or or_3 (Y, and_7_out, and_8_out);
  or or_4 (Z, and_9_out, and_10_out, A);
endmodule

module Assignment_5 (
  input  A,
  input  B,
  input  C,
  input  D,
  output W,
  output X,
  output Y,
  output Z
);

  wire and_1_out, and_2_out, and_3_out, and_4_out, and_5_out, and_6_out, and_7_out, and_8_out, and_9_out,
       and_10_out, and_11_out, and_12_out, and_13_out, and_14_out, not_1_out, not_2_out, not_3_out,
       not_4_out, not_5_out, not_6_out, not_7_out, not_8_out, not_9_out, not_10_out, not_11_out, not_12_out,
       not_13_out, not_14_out, not_15_out, not_16_out, not_17_out, not_18_out, not_19_out, not_20_out,
       not_21_out, not_22_out, not_23_out, not_24_out, not_25_out, not_26_out;

  not not_1 (not_1_out, A);
  not not_2 (not_2_out, A);
  not not_3 (not_3_out, A);
  not not_4 (not_4_out, B);
  not not_5 (not_5_out, C);
  not not_6 (not_6_out, D);
  not not_7 (not_7_out, A);
  not not_8 (not_8_out, C);
  not not_9 (not_9_out, D);
  not not_10 (not_10_out, A);
  not not_11 (not_11_out, A);
  not not_12 (not_12_out, D);
  not not_13 (not_13_out, B);
  not not_14 (not_14_out, C);
  not not_15 (not_15_out, B);
  and and_1 (and_1_out, not_15_out, not_16_out, not_17_out);
  not not_16 (not_16_out, C);
  not not_17 (not_17_out, D);
  not not_18 (not_18_out, A);
  and and_2 (and_2_out, not_18_out, B, not_19_out);
  not not_19 (not_19_out, C);
  not not_20 (not_20_out, A);
  and and_3 (and_3_out, not_20_out, B, D);
  not not_21 (not_21_out, A);
  and and_4 (and_4_out, not_21_out, not_22_out, not_23_out);
  not not_22 (not_22_out, B);
  not not_23 (not_23_out, D);
  not not_24 (not_24_out, A);
  and and_5 (and_5_out, not_24_out, B, C);
  and and_6 (and_6_out, A, not_25_out, not_26_out);
  not not_25 (not_25_out, B);
  not not_26 (not_26_out, C);
  and and_7 (and_7_out, not_1_out, D);
  and and_8 (and_8_out, not_2_out, C);
  and and_9 (and_9_out, not_3_out, B);
  and and_10 (and_10_out, A, not_4_out, not_5_out, not_6_out);
  and and_11 (and_11_out, not_7_out, not_8_out, not_9_out);
  and and_12 (and_12_out, not_10_out, C, D);
  and and_13 (and_13_out, not_11_out, B, not_12_out);
  and and_14 (and_14_out, A, not_13_out, not_14_out, D);
  or or_1 (Y, and_1_out, and_2_out, and_3_out);
  or or_2 (Z, and_4_out, and_5_out, and_6_out);
  or or_3 (W, and_7_out, and_8_out, and_9_out, and_10_out);
  or or_4 (X, and_11_out, and_12_out, and_13_out, and_14_out);
endmodule
