// Logisim project Assignment2_2.26b.circ as structural Verilog: 1 circuit, main circuit main
module main (
  input  A,
  input  B,
  input  C,
  output X
);

  and and_1 (X, A, B, C);

  // Notes on the sheet:
  //   ABC
endmodule
