// Logisim project FINAL_EXAM.circ as structural Verilog: 1 circuit, main circuit main
module main (
  input  A,
  input  B,
  input  C,
  output X,
  output Y,
  output Z
);

  wire AND_2_out, AND_3_out, not_1_out, not_2_out, not_3_out, not_4_out;

  not not_1 (not_1_out, B);
  not not_2 (not_2_out, A);
  not not_3 (not_3_out, A);
  not not_4 (not_4_out, C);
  and AND (X, A, not_1_out);
  and AND_2 (AND_2_out, not_2_out, B);
  and AND_3 (AND_3_out, not_3_out, C);
  and AND_4 (Z, A, B, not_4_out);
  or or_1 (Y, AND_2_out, AND_3_out);

  // Notes on the sheet:
  //   NOT
  //   NOT
  //   NOT
  //   NOT
endmodule
