// Logisim project FINAL_EXAM_2.circ as structural Verilog: 1 circuit, main circuit main
module main (
  input  in_1
);

  wire and_1_out, and_2_out, and_3_out, and_4_out, clock_1_out, d_ff_1_q, d_ff_2_q, d_ff_3_q, d_ff_4_q,
       not_1_out, not_2_out, not_3_out;

  Clock clock_1 (.out(clock_1_out));
  and and_1 (and_1_out, in_1, not_3_out, not_2_out, not_1_out);
  LED led_1 (.in(d_ff_1_q));
  D_Flip_Flop d_ff_1 (.clk(clock_1_out), .D(and_1_out), .Q(d_ff_1_q));  // open: Qn, preset, en, reset
  not not_1 (not_1_out, d_ff_1_q);
  and and_2 (and_2_out, d_ff_1_q, in_1);
  LED led_2 (.in(d_ff_2_q));
  D_Flip_Flop d_ff_2 (.clk(clock_1_out), .D(and_2_out), .Q(d_ff_2_q));  // open: Qn, preset, en, reset
  not not_2 (not_2_out, d_ff_2_q);
  D_Flip_Flop d_ff_3 (.clk(clock_1_out), .D(and_3_out), .Q(d_ff_3_q));  // open: Qn, preset, en, reset
  and and_3 (and_3_out, d_ff_2_q, in_1);
  LED led_3 (.in(d_ff_3_q));
  and and_4 (and_4_out, d_ff_3_q, in_1);
  not not_3 (not_3_out, d_ff_3_q);
  LED led_4 (.in(d_ff_4_q));
  D_Flip_Flop d_ff_4 (.clk(clock_1_out), .D(and_4_out), .Q(d_ff_4_q));  // open: Qn, preset, en, reset
endmodule
