// Logisim project Final.circ as structural Verilog: 1 circuit, main circuit main
module main (
  input  in_1,
  output Opened,
  output Alarm
);

  wire AND_3_out, AND_out, button_1_out, button_2_out, button_3_out, counter_1_carry, counter_2_carry,
       counter_3_carry, d_ff_1_q, d_ff_2_q, d_ff_3_q, d_ff_4_q, d_ff_5_q, not_1_out, not_2_out, not_3_out,
       not_4_out, OR_2_out, OR_out;

  Button button_1 (.out(button_1_out));
  not not_1 (not_1_out, Alarm);
  Button button_2 (.out(button_2_out));
  Button button_3 (.out(button_3_out));
  and AND (AND_out, not_1_out, button_1_out);
  D_Flip_Flop d_ff_1 (.clk(AND_out), .D(in_1), .Q(d_ff_1_q), .reset(OR_out));  // open: Qn, preset, en
  not not_2 (not_2_out, d_ff_1_q);
  or OR (OR_out, button_3_out, OR_2_out);
  D_Flip_Flop d_ff_2 (.clk(AND_out), .D(d_ff_1_q), .Q(d_ff_2_q), .reset(OR_out));  // open: Qn, preset, en
  or OR_2 (OR_2_out, Alarm, button_2_out);
  D_Flip_Flop d_ff_3 (.clk(AND_out), .D(d_ff_2_q), .Q(d_ff_3_q), .reset(OR_out));  // open: Qn, preset, en
  Counter #(.width(2), .max('h2), .ongoal("stay")) counter_1 (
    .carry(counter_1_carry), .clk(button_2_out), .clr(button_3_out));  // open: load, D, count, Q
  D_Flip_Flop d_ff_4 (.clk(AND_out), .D(d_ff_3_q), .Q(d_ff_4_q), .reset(OR_out));  // open: Qn, preset, en
  Counter #(.width(1), .max('h1), .ongoal("stay")) counter_2 (
    .carry(counter_2_carry), .clk(counter_1_carry), .clr(button_3_out));  // open: load, D, count, Q
  D_Flip_Flop d_ff_5 (.clk(AND_out), .D(d_ff_4_q), .Q(d_ff_5_q), .reset(OR_out));  // open: Qn, preset, en
  not not_3 (not_3_out, d_ff_5_q);
  and AND_2 (Alarm, counter_2_carry, counter_1_carry);
  Counter counter_3 (.carry(counter_3_carry), .clk(AND_out), .clr(OR_out));  // open: load, D, count, Q
  not not_4 (not_4_out, counter_3_carry);
  and AND_3 (AND_3_out, d_ff_4_q, d_ff_3_q, d_ff_2_q);
  and AND_4 (Opened, not_4_out, not_3_out, AND_3_out, not_2_out);

  // Notes on the sheet:
  //   Lab 8
  //   Kara Kohutek
  //   Secret Code: 001110
  //   Enter
  //   Reset
  //   Master Reset
  //   NOT
  //   NOT
  //   S0
  //   S1
  //   S2
  //   C0
  //   S3
  //   C1
  //   NOT
  //   S4
  //   S5
  //   NOT
endmodule
