// Logisim project Lab5_Task2.circ as structural Verilog: 1 circuit, main circuit main
module main (
  input  in_1,
  input  [2:0] in_2,
  output out_3,
  output out_4,
  output out_5,
  output out_6,
  output out_7
);

  Decoder #(.select(3)) decoder_1 (
    .out1(out_3), .out2(out_4), .out4(out_5), .out5(out_6), .out6(out_7), .sel(in_2), .en(in_1));  // open: out0, out3, out7
endmodule
