// Logisim project XOR_AND_KK.circ as structural Verilog: 1 circuit, main circuit main
module main (
  input  A,
  input  B,
  output C,
  output S
);

  and AND (C, A, B);
  xor xor_1 (S, A, B);

  // Notes on the sheet:
  //   Kara Kohutek
  //   Lab 2: Introduction to Boolean Equations and Circuits
  //   Task 3 - XOR and AND gates
  //   XOR
endmodule
