// Logisim project gatesTestingKK.circ as structural Verilog: 1 circuit, main circuit main
module main (
  input  in_1,
  input  in_2,
  output out_3,
  output out_4,
  output nand_gate,
  output nor_gate,
  output xor_gate,
  output not_gate
);

  and and_1 (out_3, in_1, in_2);
  or or_1 (out_4, in_1, in_2);
  nand nand_1 (nand_gate, in_1, in_2);
  nor nor_1 (nor_gate, in_1, in_2);
  xor xor_1 (xor_gate, in_1, in_2);
  not not_1 (not_gate, in_1);

  // Notes on the sheet:
  //   Kara Kohutek - Lab 1: Gates Testing Excercise
  //   Standard 6 gates - testing excercise - using one set of inputs
  //   and Gate
  //   or Gate
endmodule
